# Fritzing sketch surfbrick (saved by Fritzing 0.9.2b)
breadboards: 1

parts:
  U1 = 74HC595 [package="DIP16 [THT]"]
  U3 = 7-SEGMENT-DISPLAY-1_-RED [package=7-segment-1_pth]
  Raspberry_Pi1 = Raspberry Pi B rev2
  R1 = Resistor [tolerance=±5% resistance=220 package=THT]
  R2 = Resistor [tolerance=±5% resistance=220 package=THT]
  R3 = Resistor [tolerance=±5% resistance=220 package=THT]
  R4 = Resistor [tolerance=±5% resistance=220 package=THT]
  R5 = Resistor [tolerance=±5% resistance=220 package=THT]
  R6 = Resistor [tolerance=±5% resistance=220 package=THT]
  R7 = Resistor [tolerance=±5% resistance=220 package=THT]
  R8 = Resistor [tolerance=±5% resistance=220 package=THT]
  U5 = 74HC595 [package="DIP16 [THT]"]
  U6 = 7-SEGMENT-DISPLAY-1_-RED [package=7-segment-1_pth]
  R9 = Resistor [tolerance=±5% resistance=220 package=THT]
  R10 = Resistor [tolerance=±5% resistance=220 package=THT]
  R11 = Resistor [tolerance=±5% resistance=220 package=THT]
  R12 = Resistor [tolerance=±5% resistance=220 package=THT]
  R13 = Resistor [tolerance=±5% resistance=220 package=THT]
  R14 = Resistor [tolerance=±5% resistance=220 package=THT]
  R15 = Resistor [tolerance=±5% resistance=220 package=THT]
  R16 = Resistor [tolerance=±5% resistance=220 package=THT]

nets:
  N1: U1.Q1, R2.Pin_0
  N2: U1.Q2, R3.Pin_0
  N3: U1.Q3, R4.Pin_0
  N4: U1.Q4, R5.Pin_0
  N5: U1.Q5, R6.Pin_0
  N6: U1.Q6, R7.Pin_0
  N7: U1.Q7, R8.Pin_0
  GND: U1.GND, Raspberry_Pi1.GND, U5.GND
  N8: U1.Q7', U5.DS
  N9: U1.SH_CP, Raspberry_Pi1.GPIO_17, U5.SH_CP
  N10: U1.ST_CP, Raspberry_Pi1.GPIO_18, U5.ST_CP
  N11: U1.DS, Raspberry_Pi1.GPIO_25
  N12: U1.Q0, R1.Pin_0
  N13: U3.E, R5.Pin_1
  N14: U3.D, R4.Pin_1
  N15: U3.G1, Raspberry_Pi1.5V, U6.G1
  N16: U3.C, R3.Pin_1
  N17: U3.DP, R8.Pin_1
  N18: U3.B, R2.Pin_1
  N19: U3.A, R1.Pin_1
  N20: U3.F, R6.Pin_1
  N21: U3.G, R7.Pin_1
  N22: U5.Q1, R10.Pin_0
  N23: U5.Q2, R11.Pin_0
  N24: U5.Q3, R12.Pin_0
  N25: U5.Q4, R13.Pin_0
  N26: U5.Q5, R14.Pin_0
  N27: U5.Q6, R15.Pin_0
  N28: U5.Q7, R16.Pin_0
  N29: U5.Q0, R9.Pin_0
  N30: U6.E, R13.Pin_1
  N31: U6.D, R12.Pin_1
  N32: U6.C, R11.Pin_1
  N33: U6.DP, R16.Pin_1
  N34: U6.B, R10.Pin_1
  N35: U6.A, R9.Pin_1
  N36: U6.F, R14.Pin_1
  N37: U6.G, R15.Pin_1
